# Fritzing sketch Magic Gun - RFM69 and DFPlayer (saved by Fritzing 0.9.10b)

parts:
  Part1 = Adafruit Feather RP2040 RFM [part_number="Adafruit #5712"]
  Part2 = 12 NeoPixel Ring [part_number=1643]
  Adafruit_5x5_NeoPixel_Grid_BFF1 = Adafruit 5x5 NeoPixel Grid BFF [part_number=#5646]
  S3 = Tactile Switch Buttons - 12mm Square [package=tactile-pth-12mm]
  S4 = Tactile Switch Buttons - 12mm Square [package=tactile-pth-12mm]
  S5 = Tactile Switch Buttons - 12mm Square [package=tactile-pth-12mm]
  Part3 = Adafruit LIS3DH Triple-Axis Accelerometer [part_number="Adafruit #2809"]
  Adafruit#1 = Adafruit DRV2605L Haptic Motor Controller - STEMMA QT [part_number=2305]
  Adafruit_High_Power_Infrared_LED_Emitter1 = Adafruit High Power Infrared LED Emitter - STEMMA JST PH 2mm [part_number=#5639]
  MOTOR1 = Vibration Motor
  DFRobot_DFPlayer_Mini1 = DFRobot DFPlayer Mini [part_number=DFR0299]
  SP1 = SPEAKER [package=pcb_mount_speaker]
  S6 = Toggle Switch [package=THT]
  Part4 = Lithium Ion Cylindrical Battery 3.7v 2200mAh [part_number=1781]
  IR1 = TSOP312.., 314.. [package=THT]
  LED2 = LED - 5mm [color="Infrared (940nm)" current=0.030 package="5 mm [THT]"]

nets:
  GND: Part1.GND, Part3.GND, Adafruit#1.GND, Part4.negative
  VCC: Part1.+3V3, Part3.VCC, Adafruit#1.VCC, IR1.Data
  N1: Part1.SDA, Part3.SDA, Adafruit#1.SDA
  N2: Part1.SCL, Part3.SCL, Adafruit#1.SCL
  N3: Part1.TX, DFRobot_DFPlayer_Mini1.RX
  N4: Part1.RX, DFRobot_DFPlayer_Mini1.TX
  N5: Part1.D25, S4.1, S4.3
  N6: Part1.D24, S3.1, S3.3
  N7: Part1.A3, Adafruit_High_Power_Infrared_LED_Emitter1.SIGNAL
  N8: Part1.A2, IR1.GND
  N9: Part1.A1, S5.2, S5.4
  N10: Part1.VBAT, S6.L2
  N11: Part1.D10, Adafruit_5x5_NeoPixel_Grid_BFF1.A3
  N12: Part1.D5, Part2.IN
  N13: Adafruit_5x5_NeoPixel_Grid_BFF1.GND, S3.4, S4.4
  N14: Adafruit#1.OUT+, MOTOR1.NEG
  N15: Adafruit#1.OUT-, MOTOR1.POS
  N16: Adafruit_High_Power_Infrared_LED_Emitter1.A, LED2.cathode
  N17: Adafruit_High_Power_Infrared_LED_Emitter1.K, LED2.anode
  N18: DFRobot_DFPlayer_Mini1.SPK_1, SP1.-
  N19: DFRobot_DFPlayer_Mini1.GND-1, DFRobot_DFPlayer_Mini1.GND-2, SP1.+
  N20: S6.COM, Part4.positive

custom parts:
  Adafruit Feather RP2040 RFM: This is the Adafruit Feather RP2040 RFM. We call these RadioFruits, our take on an microcontroller with packet radio transceiver with built-in USB and battery charging. It's an Adafruit Feather RP2040 with a radio module cooked in! Great for making wireless networks that are more flexible than Bluetooth LE and without the high power requirements of WiFi. Feather is the development board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
  12 NeoPixel Ring: 12 ultra bright smart LED NeoPixels are arranged in a circle with 1.5" (37mm) outer diameter. The rings are 'chainable' - connect the output pin of one to the input pin of another. Use only one microcontroller pin to control as many as you can chain together! Each LED is addressable as the driver chip is inside the LED. Each one has ~18mA constant current drive so the color will be very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
  Adafruit 5x5 NeoPixel Grid BFF: Our QT Py boards are a great way to make very small microcontroller projects that pack a ton of power - and now we have a way for you to quickly add a glittering grid of 25 RGB addressable micro NeoPixels. It's an excellent way to make tiny wearable, cosplay, or IoT projects with dazzling LEDs. We call this the Adafruit 5x5 NeoPixel Grid BFF - a "Best Friend Forever". When you were a kid you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
  Tactile Switch Buttons - 12mm Square: Medium-sized clicky momentary switches are standard input "buttons" on electronic projects. These work best in a PCB but can be used on a solderless breadboard as shown in this tutorial. The pins are normally open (disconnected) and when the button is pressed they are momentarily closed. They come in a pack of 10, they're pretty handy so you'll want to keep them around. You can find an EAGLE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
  Adafruit LIS3DH Triple-Axis Accelerometer: The LIS3DH is a very popular low power triple-axis accelerometer. It's low-cost, but has just about every 'extra' you'd want in an accelerometer: Three axis sensing, 10-bit precision ±2g/±4g/±8g/±16g selectable scaling Both I2C (2 possible addresses) and SPI interface options Interrupt output Multiple data rate options 1 Hz to 5Khz As low as 2uA current draw (just the chip itself, not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
  Adafruit DRV2605L Haptic Motor Controller - STEMMA QT: The DRV2605 from TI is a fancy little motor driver. Rather than controlling a stepper motor or DC motor, its designed specifically for controlling haptic motors - buzzers and vibration motors. Normally one would just turn those kinds of motors on and off, but this driver has the ability to have various effects when driving a vibe motor. For example, ramping the vibration level up and down,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
  Adafruit High Power Infrared LED Emitter - STEMMA JST PH 2mm: *pew* *pew*! This board is like a little ray gun for infrared light, with two high powered LED outputs. When controlled with the onboard N-Channel FET driver, you'll be blasting 100mA-200mA of current pulsing through each LED for 10+ meters of range! This is the easiest way to get great IR emitter range without wiring up a bunch of parts. By using a 2mm pitch STEMMA JST PH cable with headers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
  Vibration Motor: An eccentric vibration motor!
  Lithium Ion Cylindrical Battery 3.7v 2200mAh: This lithium ion battery has a capacity of 2200mAh and a protection circuit that provides over-voltage, under-voltage and over-current protection. This cell can provide 2C of peak current (4400mA). Note that these batteries are not designed to sustain such high loads, we suggest keeping any constant current draw under about 0.5C (1 Amp).
